# Fritzing sketch OpenMacroRail (saved by Fritzing 0.8.7b)
breadboards: 1

parts:
  IC1 = ULN2803A [package=THT]
  TRS1 = Audio Jack (TRS) 3.5mm [package="PG203J [THT]"]
  J1 = male pin header, 5 pins [form="♂ (male)"]
  IC2 = CNY 74-2 [package=dip08]
  CNY74-1 = CNY74-4
  Shield = Arduino Uno (Rev3)
  Power_plug1 = Power plug
  U1 = Voltage Regulator - 5V [package="TO220 [THT]"]

nets:
  N1: IC1.In_1, IC1.In_2, CNY74-1.T4-E
  N2: IC1.In_3, IC1.In_4, CNY74-1.T3-E
  N3: IC1.In_5, IC1.In_6, CNY74-1.T2-E
  N4: IC1.In_7, IC1.In_8, CNY74-1.T1-E
  GND: IC1.0V, Power_plug1.GND, U1.GND
  N5: IC1.COM_-_Common, CNY74-1.T4-C, CNY74-1.T3-C, CNY74-1.T2-C, CNY74-1.T1-C, U1.output_voltage
  N6: IC1.Out_8, IC1.Out_7, J1.pin2
  N7: IC1.Out_6, IC1.Out_5, J1.pin3
  N8: IC1.Out_4, IC1.Out_3, J1.pin4
  N9: IC1.Out_2, IC1.Out_1, J1.pin5
  N10: TRS1.Sleeve, IC2.T2-C, IC2.T1-C
  N11: TRS1.Ring, IC2.T2-E
  N12: TRS1.Tip, IC2.T1-E
  N13: J1.pin1, Power_plug1.VCC, U1.input_voltage
  N14: IC2.D1-A, Shield.D13/SCK
  N15: IC2.D1-C, IC2.D2-C, CNY74-1.D1-C, CNY74-1.D2-C, CNY74-1.D3-C, CNY74-1.D4-C, Shield.GND
  N16: IC2.D2-A, Shield.D12/MISO
  N17: CNY74-1.D1-A#0, Shield.D2
  N18: CNY74-1.D1-A#3, Shield.D3_PWM
  N19: CNY74-1.D3-A, Shield.D4
  N20: CNY74-1.D4-A, Shield.D5_PWM

notes:
  OpenMacroRail

custom parts:
  CNY 74-2: CNY 74-2 Dual Opto Coupler
  : Multichannel Optocoupler with Phototransistor Output
